# Fritzing sketch AhoyWemosD1 (saved by Fritzing 0.9.10b)
circuit board: 8.46667cm x 5.64444cm

parts:
  ESP8266 = WeMos D1 Mini
  part = NRF24L01+ Breakout Board

nets:
  3V3: ESP8266.3V3, part.VCC
  N1: ESP8266.D3, part.IRQ
  N2: ESP8266.D4, part.CE
  N3: ESP8266.D5, part.SCK
  N4: ESP8266.D6, part.MISO
  N5: ESP8266.D7, part.MOSI
  N6: ESP8266.D8, part.CS
  N7: ESP8266.G, part.GND
