# Fritzing sketch Arduino_nRF24L01+ (saved by Fritzing 0.9.3b)

parts:
  Part2 = Arduino Uno (Rev3)
  Part1 = NRF24L01+ Breakout Board

nets:
  N1: Part2.D8, Part1.CS
  N2: Part2.D11_PWM/MOSI, Part1.MOSI
  N3: Part2.D12/MISO, Part1.MISO
  N4: Part2.D13/SCK, Part1.SCK
  GND: Part2.GND, Part1.GND
  N5: Part2.D7, Part1.CE
  3V3: Part2.3V3, Part1.VCC
