# Fritzing sketch ESP8266_nRF24L01+ (saved by Fritzing 0.9.3b)

parts:
  U1 = NodeMCU V3.0
  Part1 = NRF24L01+ Breakout Board

nets:
  N1: U1.D2, Part1.CS
  N2: U1.D4, Part1.CE
  3V3: U1.3V3, Part1.VCC
  N3: U1.D5, Part1.SCK
  N4: U1.D6, Part1.MISO
  N5: U1.D7, Part1.MOSI
  GND: U1.GND, Part1.GND

custom parts:
  NodeMCU V3.0: ESP8266 based NodeMCU
