# Fritzing sketch RasPi_nRF24L01+ (saved by Fritzing 0.9.3b)

parts:
  Part1 = NRF24L01+ Breakout Board
  C1 = Electrolytic Capacitor [capacitance=100µF package="100 mil [THT, electrolytic]"]
  Raspberry_Pi1 = Raspberry Pi 3 [part_number=RPI-3-V1.2]

nets:
  GND: Part1.GND, C1.-, Raspberry_Pi1.GND
  VCC: Part1.VCC, C1.+, Raspberry_Pi1.3v3
  N1: Part1.CE, Raspberry_Pi1.GIPO22
  N2: Part1.CS, Raspberry_Pi1.GIPO8
  N3: Part1.SCK, Raspberry_Pi1.GIPO11
  N4: Part1.MOSI, Raspberry_Pi1.GIPO10
  N5: Part1.MISO, Raspberry_Pi1.GIPO9
