# Fritzing sketch esp32-38-nrf_cmt (saved by Fritzing 1.0.1rc)

parts:
  U2 = CMT2300A E49 900M20S [part_number=Radio868Mhz]
  U1 = ESP32-38PinWide [part_number=ESP32-38Pin]
  ANT1 = Antenna
  U3 = NRF24L01+ Breakout Board [part_number="Radio 2.4GHz"]
  C1 = Electrolytic Capacitor [capacitance=470µF voltage=6.3V package="1010 [SMD, electrolytic]"]

nets:
  GND: U2.GND, U1.GND, U3.GND, C1.-
  N1: U2.GPIO3, U1.GPIO34
  VCC: U2.VCC, U1.3.3, U3.VCC, C1.+
  N2: U2.SCLK, U1.GPIO12
  N3: U2.SDIO, U1.GPIO14
  N4: U2.CSB, U1.GPIO27
  N5: U2.FCSB, U1.GPIO26
  N6: U2.ANT, ANT1.antenna_lead
  N7: U1.GPIO4, U3.CE
  N8: U1.GPIO16, U3.IRQ
  N9: U1.GPIO5, U3.CS
  N10: U1.GPIO18, U3.SCK
  N11: U1.GPIO19, U3.MISO
  N12: U1.GPIO23, U3.MOSI

custom parts:
  CMT2300A E49 900M20S: Radio Module for 868MHz band. Used for AhoyDTU
  ESP32-38PinWide: Generic 38-Pin ESP32 with wide format (only access to one side of pins on a breadboard) based on Stephen Lilley's HiLetgo ESP-WROOM-32 ESP32 ESP-32S Development Board.
