# Fritzing sketch esp8266_nrf (saved by Fritzing 1.0.0rc)

parts:
  WeMos_D1_Mini1 = WeMos D1 Mini
  NRF24L01 = NRF24L01+ Breakout Board
  C1 = Electrolytic Capacitor [capacitance=1µF voltage=35V package="100 mil [THT, electrolytic]"]

nets:
  3V3: WeMos_D1_Mini1.3V3, NRF24L01.VCC, C1.+
  N1: WeMos_D1_Mini1.D3, NRF24L01.CE
  N2: WeMos_D1_Mini1.D4, NRF24L01.IRQ
  N3: WeMos_D1_Mini1.D5, NRF24L01.SCK
  N4: WeMos_D1_Mini1.D6, NRF24L01.MISO
  N5: WeMos_D1_Mini1.D7, NRF24L01.MOSI
  N6: WeMos_D1_Mini1.D8, NRF24L01.CS
  N7: WeMos_D1_Mini1.G, NRF24L01.GND, C1.-
