# Fritzing sketch esp32-38-cmt (saved by Fritzing 1.0.0rc)

parts:
  U2 = CMT2300A E49 900M20S [part_number=Radio]
  U1 = ESP32-38PinWide [part_number=ESP32-38Pin]
  ANT1 = Antenna

nets:
  GND: U2.GND, U1.GND
  N1: U2.GPIO3, U1.GPIO34
  N2: U2.VCC, U1.3.3
  N3: U2.SCLK, U1.GPIO14
  N4: U2.SDIO, U1.GPIO13
  N5: U2.CSB, U1.GPIO27
  N6: U2.FCSB, U1.GPIO26
  N7: U2.ANT, ANT1.antenna_lead

custom parts:
  CMT2300A E49 900M20S: Radio Module for 868MHz band. Used for AhoyDTU
  ESP32-38PinWide: Generic 38-Pin ESP32 with wide format (only access to one side of pins on a breadboard) based on Stephen Lilley's HiLetgo ESP-WROOM-32 ESP32 ESP-32S Development Board.
