# Fritzing sketch esp32-38_nrf_ssd1306 (saved by Fritzing 1.0.0rc)

parts:
  Squix1 = OLED 0.96" 128x64 I2C SSD1306
  NRF24 = NRF24L01+ Breakout Board
  part = ESP32-38PinWide [part_number=ESP32-38PinWide]
  C1 = Electrolytic Capacitor [capacitance=1µF voltage=35V package="100 mil [THT, electrolytic]"]

nets:
  VCC: Squix1.VCC, NRF24.VCC, part.3.3, C1.+
  GND: Squix1.GND, NRF24.GND, part.GND, C1.-
  N1: Squix1.SCL, part.GPIO22
  N2: Squix1.SCA, part.GPIO21
  N3: NRF24.CE, part.GPIO4
  N4: NRF24.CS, part.GPIO5
  N5: NRF24.SCK, part.GPIO18
  N6: NRF24.MOSI, part.GPIO23
  N7: NRF24.MISO, part.GPIO19
  N8: NRF24.IRQ, part.GPIO16

custom parts:
  ESP32-38PinWide: Generic 38-Pin ESP32 with wide format (only access to one side of pins on a breadboard) based on Stephen Lilley's HiLetgo ESP-WROOM-32 ESP32 ESP-32S Development Board.
