# Fritzing sketch esp8266_nrf_ssd1306 (saved by Fritzing 1.0.0rc)

parts:
  WeMos_D1_Mini1 = WeMos D1 Mini
  NRF24L01 = NRF24L01+ Breakout Board
  C1 = Electrolytic Capacitor [capacitance=1µF voltage=35V package="100 mil [THT, electrolytic]"]
  SSD1306 = OLED 0.96" 128x64 I2C SSD1306

nets:
  VCC: WeMos_D1_Mini1.3V3, NRF24L01.VCC, C1.+, SSD1306.VCC
  N1: WeMos_D1_Mini1.D1, SSD1306.SCL
  N2: WeMos_D1_Mini1.D2, SSD1306.SCA
  N3: WeMos_D1_Mini1.D3, NRF24L01.CE
  N4: WeMos_D1_Mini1.D4, NRF24L01.IRQ
  N5: WeMos_D1_Mini1.D5, NRF24L01.SCK
  N6: WeMos_D1_Mini1.D6, NRF24L01.MISO
  N7: WeMos_D1_Mini1.D7, NRF24L01.MOSI
  N8: WeMos_D1_Mini1.D8, NRF24L01.CS
  GND: WeMos_D1_Mini1.G, NRF24L01.GND, C1.-, SSD1306.GND
